# Fritzing sketch prototype (saved by Fritzing 0.9.3b)
breadboards: 1

parts:
  U1 = ESP32-38PinWide [part_number=ESP32-38PinWide]
  DHT11_-_TEMP/UMID = DHT11 Humitidy and Temperature Sensor
  Comparador = LM393 [package=so08]
  Umidade_do_solo = Soil Moisture Sensor
  Temperatura_do_solo_para_protóripo = DS18B20 1-Wire Temperature Sensor [part_number=DS18B20]
  2_Módulo_Relé = 2 Channel Power Relay
  POWER_12V = Power Jack [package=power_jack_smd]

nets:
  VDD: U1.GPIO6, Comparador.G2_OUT, Temperatura_do_solo_para_protóripo.VDD, 2_Módulo_Relé.VCC
  GND: U1.GPIO7, Comparador.G2_+IN, Temperatura_do_solo_para_protóripo.GND, 2_Módulo_Relé.GND
  N1: U1.GPIO15, Temperatura_do_solo_para_protóripo.DQ
  N2: U1.GPIO2, Comparador.G2_-IN
  N3: U1.GPIO4, DHT11_-_TEMP/UMID.DATA
  N4: U1.GPIO5, 2_Módulo_Relé.IN1
  N5: U1.GPIO18, 2_Módulo_Relé.IN2
  N6: Comparador.G1_-IN, Umidade_do_solo.VCC
  N7: Comparador.G1_+IN, Umidade_do_solo.SIG
  N8: 2_Módulo_Relé.K2-COM, POWER_12V.GND
  N9: 2_Módulo_Relé.K2-NO, POWER_12V.GNDBREAK

custom parts:
  ESP32-38PinWide: Generic 38-Pin ESP32 with wide format (only access to one side of pins on a breadboard) based on Stephen Lilley's HiLetgo ESP-WROOM-32 ESP32 ESP-32S Development Board.
  DHT11 Humitidy and Temperature Sensor: DHT11 Humidity and Temperature Sensor
  2 Channel Power Relay: A 2 channel power relay. The module operates at 5V.
